// Logisim project 2_10 copy.circ as structural Verilog: 1 circuit, main circuit main
module main (
  input  X0,
  input  X1,
  output out_3
);

  wire nand_1_out, nand_2_out, nand_3_out, nand_4_out;

  nand nand_1 (nand_1_out, X0, X0);
  nand nand_2 (nand_2_out, X1, X1);
  nand nand_3 (nand_3_out, X0, nand_2_out);
  nand nand_4 (nand_4_out, X1, nand_1_out);
  nand nand_5 (out_3, nand_3_out, nand_4_out);
endmodule
