// Logisim project 2_5 copy.circ as structural Verilog: 1 circuit, main circuit main
module main (
  input  x,
  input  y,
  input  z,
  input  in_4,
  input  in_5,
  input  in_6,
  output out_7,
  output out_8
);

  wire and_1_out, and_2_out, nand_1_out, nand_2_out, nand_3_out, not_1_out;

  not not_1 (not_1_out, y);
  nand nand_1 (nand_1_out, in_5, in_5);
  and and_1 (and_1_out, x, not_1_out);
  and and_2 (and_2_out, y, z);
  nand nand_2 (nand_2_out, in_4, nand_1_out);
  nand nand_3 (nand_3_out, in_5, in_6);
  or or_1 (out_7, and_1_out, and_2_out);
  nand nand_4 (out_8, nand_2_out, nand_3_out);
endmodule
