// Logisim project 3_12.circ as structural Verilog: 1 circuit, main circuit main
module main (
  input  a,
  input  b,
  output out_3
);

  wire adder_1_cout, adder_1_out, and_1_out, multiplexer_1_out, multiplexer_3_out, subtractor_1_bout,
       subtractor_1_out, undriven, undriven_2, xor_1_out;

  xor xor_1 (xor_1_out, a, b);
  and and_1 (and_1_out, a, b);
  Multiplexer #(.enable("false")) multiplexer_1 (
    .in0(xor_1_out), .in1(and_1_out), .out(multiplexer_1_out), .sel(undriven));
  Adder #(.width(1)) adder_1 (.a(b), .b(a), .out(adder_1_out), .cout(adder_1_cout));  // open: cin
  Multiplexer #(.enable("false")) multiplexer_2 (
    .in0(multiplexer_1_out), .in1(multiplexer_3_out), .out(out_3));  // open: sel
  Multiplexer #(.enable("false")) multiplexer_3 (
    .in0(adder_1_cout), .in1(subtractor_1_bout), .out(multiplexer_3_out), .sel(undriven_2));
  Subtractor #(.width(1)) subtractor_1 (.a(a), .b(b), .out(subtractor_1_out), .bout(subtractor_1_bout));  // open: bin
endmodule
