// Logisim project 3_3.circ as structural Verilog: 1 circuit, main circuit main
module main (
  input  c_in,
  input  a,
  input  b,
  input  in_4,
  input  in_5,
  input  in_6,
  output c_out,
  output out_8
);

  wire and_1_out, and_2_out, nor_1_out, nor_2_out, nor_3_out, nor_4_out, not_1_out, not_2_out, xor_1_out;

  xor xor_1 (xor_1_out, a, b);
  and and_1 (and_1_out, a, b);
  nor nor_1 (nor_1_out, in_5, in_6);
  not not_1 (not_1_out, in_5);
  not not_2 (not_2_out, in_6);
  and and_2 (and_2_out, c_in, xor_1_out);
  nor nor_2 (nor_2_out, not_1_out, not_2_out);
  or or_1 (c_out, and_2_out, and_1_out);
  nor nor_3 (nor_3_out, in_4, nor_1_out);
  nor nor_4 (nor_4_out, nor_3_out, nor_2_out);
  not not_3 (out_8, nor_4_out);
endmodule
