// Logisim project 5_17.circ as structural Verilog: 1 circuit, main circuit main
module main (
  input  in_1,
  output q2,
  output q3,
  output q1,
  output q0
);

  wire and_1_out, clock_1_out, not_1_out, not_2_out, not_3_out;

  Clock clock_1 (.out(clock_1_out));
  J_K_Flip_Flop j_k_ff_1 (.J(in_1), .clk(clock_1_out), .K(in_1), .Q(q0), .reset(and_1_out));  // open: Qn, preset
  not not_1 (not_1_out, q0);
  J_K_Flip_Flop j_k_ff_2 (.J(in_1), .clk(not_1_out), .K(in_1), .Q(q1), .reset(and_1_out));  // open: Qn, preset
  not not_2 (not_2_out, q1);
  J_K_Flip_Flop j_k_ff_3 (.J(in_1), .clk(not_2_out), .K(in_1), .Q(q2), .reset(and_1_out));  // open: Qn, preset
  J_K_Flip_Flop j_k_ff_4 (.J(in_1), .clk(not_3_out), .K(in_1), .Q(q3), .reset(and_1_out));  // open: Qn, preset
  not not_3 (not_3_out, q2);
  and and_1 (and_1_out, q3, q1, q0);

  // Notes on the sheet:
  //   Reset
endmodule
