// Logisim project 5_8.circ as structural Verilog: 1 circuit, main circuit main
module main (
  input  x,
  output z
);

  wire and_1_out, and_2_out, clock_1_out, d_ff_1_q, d_ff_1_qn, d_ff_2_q, d_ff_2_qn, not_1_out, or_1_out;

  Clock clock_1 (.out(clock_1_out));
  D_Flip_Flop d_ff_1 (.clk(clock_1_out), .D(x), .Q(d_ff_1_q), .Qn(d_ff_1_qn));  // open: preset, reset
  not not_1 (not_1_out, x);
  and and_1 (and_1_out, d_ff_2_qn, d_ff_1_qn, not_1_out);
  and and_2 (and_2_out, x, d_ff_1_qn, d_ff_2_q);
  or or_1 (or_1_out, and_1_out, and_2_out);
  D_Flip_Flop d_ff_2 (.clk(clock_1_out), .D(or_1_out), .Q(d_ff_2_q), .Qn(d_ff_2_qn));  // open: preset, reset
  and and_3 (z, d_ff_1_q, d_ff_2_q);
endmodule
