// Logisim project ADD12.circ as structural Verilog: 1 circuit, main circuit main
module main (
  input  c_in
);

  wire and_1_out, and_2_out, and_3_out, and_4_out, and_5_out, and_6_out, and_7_out, and_8_out, and_9_out,
       and_10_out, and_11_out, and_12_out, and_13_out, and_14_out, and_15_out, and_16_out, and_17_out,
       and_18_out, and_19_out, and_20_out, and_21_out, and_22_out, and_23_out, and_24_out, and_25_out,
       and_26_out, and_27_out, and_28_out, and_29_out, and_30_out, and_31_out, and_32_out, and_33_out,
       and_34_out, and_35_out, and_36_out, and_37_out, and_38_out, and_39_out, and_40_out, and_41_out,
       and_42_out, and_43_out, and_44_out, and_45_out, and_46_out, and_47_out, and_48_out, and_49_out,
       and_50_out, and_51_out, and_52_out, and_53_out, and_54_out, dipswitch_1_p1, dipswitch_1_p2,
       dipswitch_1_p3, dipswitch_1_p4, dipswitch_1_p5, dipswitch_1_p6, dipswitch_1_p7, dipswitch_1_p8,
       dipswitch_1_p9, dipswitch_1_p10, dipswitch_1_p11, dipswitch_1_p12, dipswitch_2_p1, dipswitch_2_p2,
       dipswitch_2_p3, dipswitch_2_p4, dipswitch_2_p5, dipswitch_2_p6, dipswitch_2_p7, dipswitch_2_p8,
       dipswitch_2_p9, dipswitch_2_p10, dipswitch_2_p11, dipswitch_2_p12, or_1_out, or_2_out, or_3_out,
       or_4_out, or_5_out, or_6_out, or_7_out, or_8_out, or_9_out, or_10_out, or_11_out, or_12_out,
       xor_1_out, xor_2_out, xor_3_out, xor_4_out, xor_5_out, xor_6_out, xor_7_out, xor_8_out, xor_9_out,
       xor_10_out, xor_11_out, xor_12_out, xor_13_out, xor_14_out, xor_15_out, xor_16_out, xor_17_out,
       xor_18_out, xor_19_out, xor_20_out, xor_21_out, xor_22_out, xor_23_out, xor_24_out, xor_25_out,
       xor_26_out;

  // DipSwitch #(.number(12)) dipswitch_1: pin names not known; wires that end beside it: dipswitch_1_p1, dipswitch_1_p2, dipswitch_1_p3, dipswitch_1_p4, dipswitch_1_p5, dipswitch_1_p6, dipswitch_1_p7, dipswitch_1_p8, dipswitch_1_p9, dipswitch_1_p10, dipswitch_1_p11, dipswitch_1_p12
  xor xor_1 (xor_1_out, dipswitch_1_p1, dipswitch_1_p7);
  and and_1 (and_1_out, dipswitch_1_p1, dipswitch_1_p7);
  xor xor_2 (xor_2_out, dipswitch_1_p2, dipswitch_1_p8);
  and and_2 (and_2_out, dipswitch_1_p2, dipswitch_1_p8);
  buf xor_3 (xor_3_out, dipswitch_1_p3);  // XOR_Gate
  and and_3 (and_3_out, dipswitch_1_p3, dipswitch_1_p9);
  xor xor_4 (xor_4_out, dipswitch_1_p4, dipswitch_1_p10);
  and and_4 (and_4_out, dipswitch_1_p10, dipswitch_1_p4);
  xor xor_5 (xor_5_out, dipswitch_1_p5, dipswitch_1_p11);
  and and_5 (and_5_out, dipswitch_1_p11, dipswitch_1_p5);
  xor xor_6 (xor_6_out, dipswitch_1_p12, dipswitch_1_p6);
  and and_6 (and_6_out, dipswitch_1_p12, dipswitch_1_p6);
  and and_7 (and_7_out, c_in, xor_1_out);
  and and_8 (and_8_out, c_in, xor_1_out, xor_2_out);
  and and_9 (and_9_out, xor_2_out, and_1_out);
  and and_10 (and_10_out, c_in, xor_1_out, xor_2_out, xor_3_out);
  and and_11 (and_11_out, and_1_out, xor_2_out, xor_3_out);
  and and_12 (and_12_out, and_2_out, xor_3_out);
  and and_13 (and_13_out, c_in, xor_1_out, xor_2_out, xor_3_out, xor_4_out);
  and and_14 (and_14_out, and_1_out, xor_2_out, xor_3_out, xor_4_out);
  and and_15 (and_15_out, and_2_out, xor_3_out, xor_4_out);
  and and_16 (and_16_out, and_3_out, xor_4_out);
  and and_17 (and_17_out, c_in, xor_2_out, xor_1_out, xor_3_out, xor_4_out, xor_5_out);
  and and_18 (and_18_out, and_1_out, xor_2_out, xor_3_out, xor_4_out, xor_5_out);
  and and_19 (and_19_out, and_2_out, xor_3_out, xor_4_out, xor_5_out);
  and and_20 (and_20_out, and_3_out, xor_4_out, xor_5_out);
  and and_21 (and_21_out, and_4_out, xor_5_out);
  and and_22 (and_22_out, c_in, xor_5_out, xor_4_out, xor_3_out, xor_2_out, xor_1_out, xor_6_out);
  and and_23 (and_23_out, and_1_out, xor_2_out, xor_3_out, xor_4_out, xor_5_out, xor_6_out);
  and and_24 (and_24_out, and_2_out, xor_3_out, xor_4_out, xor_5_out, xor_6_out);
  and and_25 (and_25_out, and_3_out, xor_4_out, xor_5_out, xor_6_out);
  and and_26 (and_26_out, and_4_out, xor_5_out, xor_6_out);
  and and_27 (and_27_out, and_5_out, xor_6_out);
  or or_1 (or_1_out, and_7_out, and_1_out);
  or or_2 (or_2_out, and_8_out, and_2_out, and_9_out);
  or or_3 (or_3_out, and_10_out, and_11_out, and_3_out, and_12_out);
  or or_4 (or_4_out, and_13_out, and_14_out, and_4_out, and_15_out, and_16_out);
  or or_5 (or_5_out, and_17_out, and_18_out, and_5_out, and_19_out, and_20_out, and_21_out);
  or or_6 (or_6_out, and_22_out, and_23_out, and_24_out, and_25_out, and_6_out, and_26_out, and_27_out);
  xor xor_7 (xor_7_out, c_in, xor_1_out);
  LED led_1 (.in(xor_7_out));
  xor xor_8 (xor_8_out, or_1_out, xor_2_out);
  xor xor_9 (xor_9_out, or_2_out, xor_3_out);
  LED led_2 (.in(xor_9_out));
  xor xor_10 (xor_10_out, or_3_out, xor_4_out);
  xor xor_11 (xor_11_out, or_4_out, xor_5_out);
  LED led_3 (.in(or_6_out));
  LED led_4 (.in(xor_8_out));
  LED led_5 (.in(xor_10_out));
  LED led_6 (.in(xor_11_out));
  xor xor_12 (xor_12_out, or_5_out, xor_6_out);
  LED led_7 (.in(xor_12_out));
  xor xor_13 (xor_13_out, xor_12_out, or_6_out);
  LED led_8 (.in(xor_13_out));
  // DipSwitch #(.number(12)) dipswitch_2: pin names not known; wires that end beside it: dipswitch_2_p1, dipswitch_2_p2, dipswitch_2_p3, dipswitch_2_p4, dipswitch_2_p5, dipswitch_2_p6, dipswitch_2_p7, dipswitch_2_p8, dipswitch_2_p9, dipswitch_2_p10, dipswitch_2_p11, dipswitch_2_p12
  xor xor_14 (xor_14_out, dipswitch_2_p1, dipswitch_2_p7);
  and and_28 (and_28_out, dipswitch_2_p1, dipswitch_2_p7);
  xor xor_15 (xor_15_out, dipswitch_2_p2, dipswitch_2_p8);
  and and_29 (and_29_out, dipswitch_2_p2, dipswitch_2_p8);
  xor xor_16 (xor_16_out, dipswitch_2_p3, dipswitch_2_p9);
  and and_30 (and_30_out, dipswitch_2_p3, dipswitch_2_p9);
  xor xor_17 (xor_17_out, dipswitch_2_p4, dipswitch_2_p10);
  and and_31 (and_31_out, dipswitch_2_p10, dipswitch_2_p4);
  xor xor_18 (xor_18_out, dipswitch_2_p5, dipswitch_2_p11);
  and and_32 (and_32_out, dipswitch_2_p11, dipswitch_2_p5);
  xor xor_19 (xor_19_out, dipswitch_2_p12, dipswitch_2_p6);
  and and_33 (and_33_out, dipswitch_2_p12, dipswitch_2_p6);
  and and_34 (and_34_out, or_6_out, xor_14_out);
  and and_35 (and_35_out, or_6_out, xor_14_out, xor_15_out);
  and and_36 (and_36_out, xor_15_out, and_28_out);
  and and_37 (and_37_out, or_6_out, xor_14_out, xor_15_out, xor_16_out);
  and and_38 (and_38_out, and_28_out, xor_15_out, xor_16_out);
  and and_39 (and_39_out, and_29_out, xor_16_out);
  and and_40 (and_40_out, or_6_out, xor_14_out, xor_15_out, xor_16_out, xor_17_out);
  and and_41 (and_41_out, and_28_out, xor_15_out, xor_16_out, xor_17_out);
  and and_42 (and_42_out, and_29_out, xor_16_out, xor_17_out);
  and and_43 (and_43_out, and_30_out, xor_17_out);
  and and_44 (and_44_out, or_6_out, xor_15_out, xor_14_out, xor_16_out, xor_17_out, xor_18_out);
  and and_45 (and_45_out, and_28_out, xor_15_out, xor_16_out, xor_17_out, xor_18_out);
  and and_46 (and_46_out, and_29_out, xor_16_out, xor_17_out, xor_18_out);
  and and_47 (and_47_out, and_30_out, xor_17_out, xor_18_out);
  and and_48 (and_48_out, and_31_out, xor_18_out);
  and and_49 (and_49_out, or_6_out, xor_18_out, xor_17_out, xor_16_out, xor_15_out, xor_14_out, xor_19_out);
  and and_50 (and_50_out, and_28_out, xor_15_out, xor_16_out, xor_17_out, xor_18_out, xor_19_out);
  and and_51 (and_51_out, and_29_out, xor_16_out, xor_17_out, xor_18_out, xor_19_out);
  and and_52 (and_52_out, and_30_out, xor_17_out, xor_18_out, xor_19_out);
  and and_53 (and_53_out, and_31_out, xor_18_out, xor_19_out);
  and and_54 (and_54_out, and_32_out, xor_19_out);
  or or_7 (or_7_out, and_34_out, and_28_out);
  or or_8 (or_8_out, and_35_out, and_29_out, and_36_out);
  or or_9 (or_9_out, and_37_out, and_38_out, and_30_out, and_39_out);
  or or_10 (or_10_out, and_40_out, and_41_out, and_31_out, and_42_out, and_43_out);
  or or_11 (or_11_out, and_44_out, and_45_out, and_32_out, and_46_out, and_47_out, and_48_out);
  or or_12 (or_12_out, and_49_out, and_50_out, and_51_out, and_52_out, and_33_out, and_53_out, and_54_out);
  xor xor_20 (xor_20_out, or_6_out, xor_14_out);
  xor xor_21 (xor_21_out, or_7_out, xor_15_out);
  xor xor_22 (xor_22_out, or_8_out, xor_16_out);
  LED led_9 (.in(xor_22_out));
  xor xor_23 (xor_23_out, or_10_out, xor_18_out);
  LED led_10 (.in(or_12_out));
  LED led_11 (.in(xor_20_out));
  LED led_12 (.in(xor_21_out));
  xor xor_24 (xor_24_out, or_9_out, xor_17_out);
  LED led_13 (.in(xor_24_out));
  LED led_14 (.in(xor_23_out));
  xor xor_25 (xor_25_out, or_11_out, xor_19_out);
  LED led_15 (.in(xor_25_out));
  xor xor_26 (xor_26_out, xor_25_out, or_12_out);
  LED led_16 (.in(xor_26_out));

  // Notes on the sheet:
  //   a
  //   b
  //   PGU
  //   p0
  //   g0
  //   p1
  //   g1
  //   p2
  //   g2
  //   p3
  //   g3
  //   p4
  //   g4
  //   p5
  //   g5
  //   CGU
  //   c1
  //   c2
  //   c3
  //   c4
  //   c5
  //   c6
  //   SU
  //   s2
  //   c_out
  //   s0
  //   s1
  //    s3
  //   s4
  //   s5
  //   overflow
  //   a
  //   b
  //   PGU
  //   p6
  //   g6
  //   p7
  //   g7
  //   p8
  //   g8
  //   p9
  //   g9
  //   p10
  //   g10
  //   p11
  //   g11
  //   c-in
  //   CGU
  //   c7
  //   c8
  //   c9
  //   c10
  //   c11
  //   c12
  //   SU
  //   s8
  //   c_out
  //   s6
  //   s7
  //    s9
  //   s10
  //   s11
  //   overflow
endmodule
