// Logisim project C1.circ as structural Verilog: 1 circuit, main circuit main
module main (
  input  c_in,
  output c_out
);

  wire and_1_out, and_2_out, and_3_out, and_4_out, and_5_out, and_6_out, and_7_out, and_8_out, and_9_out,
       and_10_out, and_11_out, and_12_out, and_13_out, and_14_out, dipswitch_1_p1, dipswitch_1_p2,
       dipswitch_1_p3, dipswitch_1_p4, dipswitch_1_p5, dipswitch_1_p6, dipswitch_1_p7, dipswitch_1_p8,
       or_1_out, or_2_out, or_3_out, xor_1_out, xor_2_out, xor_3_out, xor_4_out, xor_5_out, xor_6_out,
       xor_7_out, xor_8_out;

  // DipSwitch dipswitch_1: pin names not known; wires that end beside it: dipswitch_1_p1, dipswitch_1_p2, dipswitch_1_p3, dipswitch_1_p4, dipswitch_1_p5, dipswitch_1_p6, dipswitch_1_p7, dipswitch_1_p8
  xor xor_1 (xor_1_out, dipswitch_1_p1, dipswitch_1_p5);
  and and_1 (and_1_out, dipswitch_1_p1, dipswitch_1_p5);
  xor xor_2 (xor_2_out, dipswitch_1_p2, dipswitch_1_p6);
  and and_2 (and_2_out, dipswitch_1_p2, dipswitch_1_p6);
  xor xor_3 (xor_3_out, dipswitch_1_p3, dipswitch_1_p7);
  and and_3 (and_3_out, dipswitch_1_p3, dipswitch_1_p7);
  xor xor_4 (xor_4_out, dipswitch_1_p4, dipswitch_1_p8);
  and and_4 (and_4_out, dipswitch_1_p8, dipswitch_1_p4);
  and and_5 (and_5_out, c_in, xor_1_out);
  and and_6 (and_6_out, c_in, xor_1_out, xor_2_out);
  and and_7 (and_7_out, xor_2_out, and_1_out);
  and and_8 (and_8_out, c_in, xor_1_out, xor_2_out, xor_3_out);
  and and_9 (and_9_out, and_1_out, xor_2_out, xor_3_out);
  and and_10 (and_10_out, and_2_out, xor_3_out);
  and and_11 (and_11_out, c_in, xor_1_out, xor_2_out, xor_3_out, xor_4_out);
  and and_12 (and_12_out, and_1_out, xor_2_out, xor_3_out, xor_4_out);
  and and_13 (and_13_out, and_2_out, xor_3_out, xor_4_out);
  and and_14 (and_14_out, and_3_out, xor_4_out);
  or or_1 (or_1_out, and_5_out, and_1_out);
  or or_2 (or_2_out, and_6_out, and_2_out, and_7_out);
  or or_3 (or_3_out, and_8_out, and_9_out, and_3_out, and_10_out);
  or or_4 (c_out, and_11_out, and_12_out, and_4_out, and_13_out, and_14_out);
  xor xor_5 (xor_5_out, c_in, xor_1_out);
  LED led_1 (.in(xor_5_out));
  xor xor_6 (xor_6_out, or_1_out, xor_2_out);
  xor xor_7 (xor_7_out, or_2_out, xor_3_out);
  LED led_2 (.in(xor_7_out));
  xor xor_8 (xor_8_out, or_3_out, xor_4_out);
  LED led_3 (.in(xor_6_out));
  LED led_4 (.in(xor_8_out));

  // Notes on the sheet:
  //   a
  //   b
  //   PGU
  //   p0
  //   g0
  //   p1
  //   g1
  //   p2
  //   g2
  //   p3
  //   g3
  //   CGU
  //   c1
  //   c2
  //   c3
  //   c4
  //   SU
  //   s2
  //   s0
  //   s1
  //    s3
endmodule
