// Logisim project CLA6.circ as structural Verilog: 1 circuit, main circuit main
module main (
  input  c_in
);

  wire and_1_out, and_2_out, and_3_out, and_4_out, and_5_out, and_6_out, and_7_out, and_8_out, and_9_out,
       and_10_out, and_11_out, and_12_out, and_13_out, and_14_out, and_15_out, and_16_out, and_17_out,
       and_18_out, and_19_out, and_20_out, and_21_out, and_22_out, and_23_out, and_24_out, and_25_out,
       and_26_out, and_27_out, dipswitch_1_p1, dipswitch_1_p2, dipswitch_1_p3, dipswitch_1_p4,
       dipswitch_1_p5, dipswitch_1_p6, dipswitch_1_p7, dipswitch_1_p8, dipswitch_1_p9, dipswitch_1_p10,
       dipswitch_1_p11, dipswitch_1_p12, or_1_out, or_2_out, or_3_out, or_4_out, or_5_out, or_6_out,
       xor_1_out, xor_2_out, xor_3_out, xor_4_out, xor_5_out, xor_6_out, xor_7_out, xor_8_out, xor_9_out,
       xor_10_out, xor_11_out, xor_12_out, xor_13_out;

  // DipSwitch #(.number(12)) dipswitch_1: pin names not known; wires that end beside it: dipswitch_1_p1, dipswitch_1_p2, dipswitch_1_p3, dipswitch_1_p4, dipswitch_1_p5, dipswitch_1_p6, dipswitch_1_p7, dipswitch_1_p8, dipswitch_1_p9, dipswitch_1_p10, dipswitch_1_p11, dipswitch_1_p12
  xor xor_1 (xor_1_out, dipswitch_1_p1, dipswitch_1_p7);
  and and_1 (and_1_out, dipswitch_1_p1, dipswitch_1_p7);
  xor xor_2 (xor_2_out, dipswitch_1_p2, dipswitch_1_p8);
  and and_2 (and_2_out, dipswitch_1_p2, dipswitch_1_p8);
  buf xor_3 (xor_3_out, dipswitch_1_p3);  // XOR_Gate
  and and_3 (and_3_out, dipswitch_1_p3, dipswitch_1_p9);
  xor xor_4 (xor_4_out, dipswitch_1_p4, dipswitch_1_p10);
  and and_4 (and_4_out, dipswitch_1_p10, dipswitch_1_p4);
  xor xor_5 (xor_5_out, dipswitch_1_p5, dipswitch_1_p11);
  and and_5 (and_5_out, dipswitch_1_p11, dipswitch_1_p5);
  xor xor_6 (xor_6_out, dipswitch_1_p12, dipswitch_1_p6);
  and and_6 (and_6_out, dipswitch_1_p12, dipswitch_1_p6);
  and and_7 (and_7_out, c_in, xor_1_out);
  and and_8 (and_8_out, c_in, xor_1_out, xor_2_out);
  and and_9 (and_9_out, xor_2_out, and_1_out);
  and and_10 (and_10_out, c_in, xor_1_out, xor_2_out, xor_3_out);
  and and_11 (and_11_out, and_1_out, xor_2_out, xor_3_out);
  and and_12 (and_12_out, and_2_out, xor_3_out);
  and and_13 (and_13_out, c_in, xor_1_out, xor_2_out, xor_3_out, xor_4_out);
  and and_14 (and_14_out, and_1_out, xor_2_out, xor_3_out, xor_4_out);
  and and_15 (and_15_out, and_2_out, xor_3_out, xor_4_out);
  and and_16 (and_16_out, and_3_out, xor_4_out);
  and and_17 (and_17_out, c_in, xor_2_out, xor_1_out, xor_3_out, xor_4_out, xor_5_out);
  and and_18 (and_18_out, and_1_out, xor_2_out, xor_3_out, xor_4_out, xor_5_out);
  and and_19 (and_19_out, and_2_out, xor_3_out, xor_4_out, xor_5_out);
  and and_20 (and_20_out, and_3_out, xor_4_out, xor_5_out);
  and and_21 (and_21_out, and_4_out, xor_5_out);
  and and_22 (and_22_out, c_in, xor_5_out, xor_4_out, xor_3_out, xor_2_out, xor_1_out, xor_6_out);
  and and_23 (and_23_out, and_1_out, xor_2_out, xor_3_out, xor_4_out, xor_5_out, xor_6_out);
  and and_24 (and_24_out, and_2_out, xor_3_out, xor_4_out, xor_5_out, xor_6_out);
  and and_25 (and_25_out, and_3_out, xor_4_out, xor_5_out, xor_6_out);
  and and_26 (and_26_out, and_4_out, xor_5_out, xor_6_out);
  and and_27 (and_27_out, and_5_out, xor_6_out);
  or or_1 (or_1_out, and_7_out, and_1_out);
  or or_2 (or_2_out, and_8_out, and_2_out, and_9_out);
  or or_3 (or_3_out, and_10_out, and_11_out, and_3_out, and_12_out);
  or or_4 (or_4_out, and_13_out, and_14_out, and_4_out, and_15_out, and_16_out);
  or or_5 (or_5_out, and_17_out, and_18_out, and_5_out, and_19_out, and_20_out, and_21_out);
  or or_6 (or_6_out, and_22_out, and_23_out, and_24_out, and_25_out, and_6_out, and_26_out, and_27_out);
  xor xor_7 (xor_7_out, c_in, xor_1_out);
  LED led_1 (.in(xor_7_out));
  xor xor_8 (xor_8_out, or_1_out, xor_2_out);
  xor xor_9 (xor_9_out, or_2_out, xor_3_out);
  LED led_2 (.in(xor_9_out));
  xor xor_10 (xor_10_out, or_3_out, xor_4_out);
  xor xor_11 (xor_11_out, or_4_out, xor_5_out);
  LED led_3 (.in(or_6_out));
  LED led_4 (.in(xor_8_out));
  LED led_5 (.in(xor_10_out));
  LED led_6 (.in(xor_11_out));
  xor xor_12 (xor_12_out, or_5_out, xor_6_out);
  LED led_7 (.in(xor_12_out));
  xor xor_13 (xor_13_out, xor_12_out, or_6_out);
  LED led_8 (.in(xor_13_out));

  // Notes on the sheet:
  //   a
  //   b
  //   PGU
  //   p0
  //   g0
  //   p1
  //   g1
  //   p2
  //   g2
  //   p3
  //   g3
  //   p4
  //   g4
  //   p5
  //   g5
  //   CGU
  //   c1
  //   c2
  //   c3
  //   c4
  //   c5
  //   c6
  //   SU
  //   s2
  //   c_out
  //   s0
  //   s1
  //    s3
  //   s4
  //   s5
  //   overflow
endmodule
