// Logisim project A1.circ as structural Verilog: 1 circuit, main circuit main
module main (
  input  in_1,
  input  in_2,
  input  in_3,
  input  in_4,
  input  in_5,
  input  in_6,
  input  in_7,
  output out_8,
  output out_9,
  output out_10,
  output out_11
);

  wire nor_3_out, nor_4_out, nor_5_out;

  nor nor_1 (out_8, in_1, in_1);
  nor nor_2 (out_9, in_2, in_3);
  nor nor_3 (nor_3_out, in_4, in_5);
  nor nor_4 (nor_4_out, in_6, in_6);
  nor nor_5 (nor_5_out, in_7, in_7);
  nor nor_6 (out_10, nor_3_out, nor_3_out);
  nor nor_7 (out_11, nor_4_out, nor_5_out);

  // Notes on the sheet:
  //   Not Gate
  //   Nor Gate
  //   Or Gate
  //   And Gate
endmodule
