// Logisim project A3.circ as structural Verilog: 1 circuit, main circuit main
module main (
  input  in_1,
  input  in_2,
  input  in_3,
  input  in_4,
  input  in_5,
  input  in_6,
  input  in_7,
  input  A,
  input  B,
  output out_10,
  output out_11,
  output out_12,
  output out_13,
  output out_14
);

  wire nor_3_out, nor_4_out, nor_5_out, nor_8_out, nor_9_out, nor_10_out, nor_11_out, nor_12_out;

  nor nor_1 (out_10, in_1, in_1);
  nor nor_2 (out_11, in_2, in_3);
  nor nor_3 (nor_3_out, in_4, in_5);
  nor nor_4 (nor_4_out, in_6, in_6);
  nor nor_5 (nor_5_out, in_7, in_7);
  nor nor_6 (out_12, nor_3_out, nor_3_out);
  nor nor_7 (out_13, nor_4_out, nor_5_out);
  nor nor_8 (nor_8_out, A, A);
  nor nor_9 (nor_9_out, B, B);
  nor nor_10 (nor_10_out, nor_8_out, B);
  nor nor_11 (nor_11_out, A, nor_9_out);
  nor nor_12 (nor_12_out, nor_10_out, nor_11_out);
  nor nor_13 (out_14, nor_12_out, nor_12_out);

  // Notes on the sheet:
  //   Not Gate
  //   Nor Gate
  //   Or Gate
  //   And Gate
  //   Not A
  //   Not B
  //   Xor Gate
endmodule
