// Logisim project A4.circ as structural Verilog: 1 circuit, main circuit main
module main (
  input  A,
  input  B,
  input  A_2,
  input  B_2,
  output out_5,
  output out_6
);

  wire nor_1_out, nor_2_out, nor_3_out, nor_4_out, nor_5_out, nor_6_out, nor_7_out, nor_8_out, nor_9_out,
       nor_10_out, nor_11_out, nor_12_out, nor_13_out, nor_14_out;

  nor nor_1 (nor_1_out, B, B);
  nor nor_2 (nor_2_out, A, A);
  nor nor_3 (nor_3_out, A, A);
  nor nor_4 (nor_4_out, nor_1_out, nor_1_out);
  nor nor_5 (nor_5_out, nor_2_out, nor_2_out);
  nor nor_6 (nor_6_out, B, B);
  nor nor_7 (nor_7_out, A_2, A_2);
  nor nor_8 (nor_8_out, B_2, B_2);
  nor nor_9 (nor_9_out, nor_3_out, nor_4_out);
  nor nor_10 (nor_10_out, nor_5_out, nor_6_out);
  nor nor_11 (nor_11_out, nor_7_out, B_2);
  nor nor_12 (nor_12_out, A_2, nor_8_out);
  nor nor_13 (nor_13_out, nor_9_out, nor_10_out);
  nor nor_14 (nor_14_out, nor_11_out, nor_12_out);
  nor nor_15 (out_5, nor_13_out, nor_13_out);
  nor nor_16 (out_6, nor_14_out, nor_14_out);

  // Notes on the sheet:
  //   Propogation Delay
  //   A = 4
  //   Not A = 5
  //   B = 4
  //   Not B = 5
  //   Propogation Delay
  //   A = 3
  //   Not A = 4
  //   B = 3
  //   Not B = 4
  //   Not A
  //   Not B
  //   Not A
  //   Not B
endmodule
