// Logisim project A5.circ as structural Verilog: 1 circuit, main circuit main
module main (
  input  w,
  input  x,
  input  y,
  input  z
);

  wire and_1_out, and_2_out, and_3_out, and_4_out, and_5_out, and_6_out, and_7_out, and_8_out, and_9_out,
       and_10_out, not_1_out, not_2_out, not_3_out, not_4_out, or_1_out, or_2_out, or_3_out, or_4_out,
       or_5_out, or_6_out, or_7_out;

  not not_1 (not_1_out, w);
  not not_2 (not_2_out, x);
  not not_3 (not_3_out, y);
  not not_4 (not_4_out, z);
  and and_1 (and_1_out, not_1_out, not_2_out, not_3_out, not_4_out);
  and and_2 (and_2_out, not_1_out, not_2_out, not_3_out, z);
  and and_3 (and_3_out, not_1_out, not_2_out, y, not_4_out);
  and and_4 (and_4_out, not_1_out, not_2_out, y, z);
  and and_5 (and_5_out, not_1_out, x, not_3_out, not_4_out);
  and and_6 (and_6_out, not_1_out, x, not_3_out, z);
  and and_7 (and_7_out, not_1_out, x, y, not_4_out);
  and and_8 (and_8_out, not_1_out, x, y, z);
  and and_9 (and_9_out, w, not_2_out, not_3_out, not_4_out);
  and and_10 (and_10_out, w, not_2_out, not_3_out, z);
  or or_1 (or_1_out, and_1_out, and_3_out, and_4_out, and_6_out, and_7_out, and_8_out, and_9_out, and_10_out);
  or or_2 (or_2_out, and_1_out, and_2_out, and_3_out, and_4_out, and_5_out, and_8_out, and_9_out, and_10_out);
  or or_3 (or_3_out, and_1_out, and_2_out, and_4_out, and_5_out, and_6_out, and_7_out, and_8_out, and_9_out, and_10_out);
  or or_4 (or_4_out, and_1_out, and_3_out, and_4_out, and_6_out, and_7_out, and_9_out, and_10_out);
  or or_5 (or_5_out, and_1_out, and_3_out, and_7_out, and_9_out);
  or or_6 (or_6_out, and_1_out, and_5_out, and_6_out, and_7_out, and_9_out, and_10_out);
  or or_7 (or_7_out, and_3_out, and_4_out, and_5_out, and_6_out, and_7_out, and_9_out, and_10_out);
  _7_Segment_Display u_7_segment_display_1 (
    .g(or_7_out), .f(or_6_out), .a(or_1_out), .b(or_2_out), .e(or_5_out), .d(or_4_out), .c(or_3_out));  // open: dp

  // Notes on the sheet:
  //   e = w'x'y'z+w'x'yz'+w'xyz'+wx'y'z'
  //   f = w'x'y'z'+w'xy'z'+w'xy'z+w'xyz'+wx'y'z'+wx'y'z
  //   a = w'x'y'z'+w'x'yz'+w'x'yz+w'xy'z+w'xyz'+w'xyz+wx'y'z'+wx'y'z
  //   b = w'x'y'z'+w'x'y'z+w'x'yz'+w'x'yz+w'xy'z'+w'xyz+wx'y'z'+wx'y'z 
  //   c = w'x'y'z'+w'x'y'z+w'x'yz+w'xy'z'+w'xy'z+w'xyz'+w'xyz+wx'y'z'+wx'y'z
  //   d = w'x'y'z'+w'x'yz'+w'x'yz+w'xy'z+w'xyz'+wx'y'z'+wx'y'z
  //   g = w'x'yz'+w'x'yz+w'xy'z'+w'xy'z+w'xyz'+wx'y'z'+wx'y'z
  //   a
  //   b
  //   c
  //   d
  //   e
  //   f
  //   g
endmodule
