// Logisim project 2_27.circ as structural Verilog: 1 circuit, main circuit main
module main (
  input  x,
  input  y,
  input  z,
  output r1,
  output r0,
  output a
);

  wire nand_2_out, nand_4_out;

  nand nand_1 (r1, x, x);
  nand nand_2 (nand_2_out, y, y);
  nand nand_3 (a, x, y, z);
  nand nand_4 (nand_4_out, x, nand_2_out);
  nand nand_5 (r0, nand_4_out, nand_4_out);
endmodule
