// Logisim project 2_7.circ as structural Verilog: 1 circuit, main circuit main
module main (
  input  x,
  input  y,
  input  z,
  input  x_2,
  input  y_2,
  input  z_2,
  output out_7,
  output out_8
);

  wire nor_1_out, nor_2_out, nor_3_out, not_1_out, or_1_out, or_2_out;

  not not_1 (not_1_out, y);
  nor nor_1 (nor_1_out, y_2, y_2);
  or or_1 (or_1_out, x, y);
  or or_2 (or_2_out, not_1_out, z);
  nor nor_2 (nor_2_out, x_2, y_2);
  nor nor_3 (nor_3_out, nor_1_out, z_2);
  and and_1 (out_7, or_1_out, or_2_out);
  nor nor_4 (out_8, nor_2_out, nor_3_out);
endmodule
