// Logisim project Lab 2 Problem 1.circ as structural Verilog: 1 circuit, main circuit main
module main (
  input  X,
  input  Y,
  input  Z,
  output Out
);

  wire nand_1_out, not_1_out, not_2_out, or_1_out;

  not not_1 (not_1_out, X);
  not not_2 (not_2_out, Z);
  or or_1 (or_1_out, not_1_out, Y);
  nand nand_1 (nand_1_out, Y, not_2_out);
  and and_1 (Out, or_1_out, nand_1_out);
endmodule
