// Logisim project Multiplier.circ as structural Verilog: 14 circuits, main circuit CLA6
module CLA6 (
  input  c_in,
  input  [5:0] in_2,
  input  [5:0] in_3,
  output [5:0] out_4,
  output out_5,
  output c_out
);

  wire and_1_out, and_2_out, and_3_out, and_4_out, and_5_out, and_6_out, and_7_out, and_8_out, and_9_out,
       and_10_out, and_11_out, and_12_out, and_13_out, and_14_out, and_15_out, and_16_out, and_17_out,
       and_18_out, and_19_out, and_20_out, and_21_out, and_22_out, and_23_out, and_24_out, and_25_out,
       and_26_out, and_27_out, or_1_out, or_2_out, or_3_out, or_4_out, or_5_out, xor_1_out, xor_2_out,
       xor_3_out, xor_4_out, xor_5_out, xor_6_out;

  // DipSwitch #(.number(6)) dipswitch_1: pin names not known
  // DipSwitch #(.number(6)) dipswitch_2: pin names not known
  xor xor_1 (xor_1_out, in_2[0], in_3[0]);
  and and_1 (and_1_out, in_2[0], in_3[0]);
  xor xor_2 (xor_2_out, in_2[1], in_3[1]);
  and and_2 (and_2_out, in_2[1], in_3[1]);
  xor xor_3 (xor_3_out, in_2[2], in_3[2]);
  and and_3 (and_3_out, in_2[2], in_3[2]);
  xor xor_4 (xor_4_out, in_2[3], in_3[3]);
  and and_4 (and_4_out, in_3[3], in_2[3]);
  xor xor_5 (xor_5_out, in_2[4], in_3[4]);
  and and_5 (and_5_out, in_3[4], in_2[4]);
  xor xor_6 (xor_6_out, in_3[5], in_2[5]);
  and and_6 (and_6_out, in_3[5], in_2[5]);
  and and_7 (and_7_out, c_in, xor_1_out);
  and and_8 (and_8_out, c_in, xor_1_out, xor_2_out);
  and and_9 (and_9_out, xor_2_out, and_1_out);
  and and_10 (and_10_out, c_in, xor_1_out, xor_2_out, xor_3_out);
  and and_11 (and_11_out, and_1_out, xor_2_out, xor_3_out);
  and and_12 (and_12_out, and_2_out, xor_3_out);
  and and_13 (and_13_out, c_in, xor_1_out, xor_2_out, xor_3_out, xor_4_out);
  and and_14 (and_14_out, and_1_out, xor_2_out, xor_3_out, xor_4_out);
  and and_15 (and_15_out, and_2_out, xor_3_out, xor_4_out);
  and and_16 (and_16_out, and_3_out, xor_4_out);
  and and_17 (and_17_out, c_in, xor_2_out, xor_1_out, xor_3_out, xor_4_out, xor_5_out);
  and and_18 (and_18_out, and_1_out, xor_2_out, xor_3_out, xor_4_out, xor_5_out);
  and and_19 (and_19_out, and_2_out, xor_3_out, xor_4_out, xor_5_out);
  and and_20 (and_20_out, and_3_out, xor_4_out, xor_5_out);
  and and_21 (and_21_out, and_4_out, xor_5_out);
  and and_22 (and_22_out, c_in, xor_5_out, xor_4_out, xor_3_out, xor_2_out, xor_1_out, xor_6_out);
  and and_23 (and_23_out, and_1_out, xor_2_out, xor_3_out, xor_4_out, xor_5_out, xor_6_out);
  and and_24 (and_24_out, and_2_out, xor_3_out, xor_4_out, xor_5_out, xor_6_out);
  and and_25 (and_25_out, and_3_out, xor_4_out, xor_5_out, xor_6_out);
  and and_26 (and_26_out, and_4_out, xor_5_out, xor_6_out);
  and and_27 (and_27_out, and_5_out, xor_6_out);
  or or_1 (or_1_out, and_7_out, and_1_out);
  or or_2 (or_2_out, and_8_out, and_2_out, and_9_out);
  or or_3 (or_3_out, and_10_out, and_11_out, and_3_out, and_12_out);
  or or_4 (or_4_out, and_13_out, and_14_out, and_4_out, and_15_out, and_16_out);
  or or_5 (or_5_out, and_17_out, and_18_out, and_5_out, and_19_out, and_20_out, and_21_out);
  or or_6 (c_out, and_22_out, and_23_out, and_24_out, and_25_out, and_6_out, and_26_out, and_27_out);
  xor xor_7 (out_4[0], c_in, xor_1_out);
  xor xor_8 (out_4[1], or_1_out, xor_2_out);
  xor xor_9 (out_4[2], or_2_out, xor_3_out);
  xor xor_10 (out_4[3], or_3_out, xor_4_out);
  xor xor_11 (out_4[4], or_4_out, xor_5_out);
  xor xor_12 (out_4[5], or_5_out, xor_6_out);
  xor xor_13 (out_5, out_4[5], c_out);

  // Notes on the sheet:
  //   a
  //   b
  //   PGU
  //   p0
  //   g0
  //   p1
  //   g1
  //   p2
  //   g2
  //   p3
  //   g3
  //   p4
  //   g4
  //   p5
  //   g5
  //   CGU
  //   c1
  //   c2
  //   c3
  //   c4
  //   c5
  //   c6
  //   SU
  //   s2
  //   s0
  //   s1
  //    s3
  //   s4
  //   s5
  //   overflow
endmodule

module ADD12 (
  input  in_1,
  input  [11:0] a,
  input  [11:0] b,
  output out_4,
  output [11:0] out_5,
  output out_6
);

  wire cla6_1_c_out, cla6_1_out_5, cla6_2_out_5;

  CLA6 cla6_1 (
    .out_5(cla6_1_out_5), .out_4(out_5[5:0]), .c_out(cla6_1_c_out), .in_2(a[5:0]), .c_in(in_1), .in_3(b[5:0]));
  CLA6 cla6_2 (
    .out_5(cla6_2_out_5), .out_4(out_5[11:6]), .c_out(out_6), .in_2(a[11:6]), .c_in(cla6_1_c_out),
    .in_3(b[11:6]));
  xor xor_1 (out_4, cla6_1_out_5, cla6_2_out_5);
endmodule

module ADDSUB12 (
  input  [11:0] in_1,
  input  s2,
  input  m,
  input  [11:0] in_4,
  output [11:0] out_5,
  output out_6,
  output out_7
);

  wire [11:0] multiplexer_1_out, xor_1_out;

  Multiplexer #(.enable("false"), .width(12)) multiplexer_1 (
    .in0(12'h1), .in1(in_1), .out(multiplexer_1_out), .sel(s2));
  xor xor_1 (xor_1_out[0], multiplexer_1_out[0], m);
  xor xor_2 (xor_1_out[1], multiplexer_1_out[1], m);
  xor xor_3 (xor_1_out[2], multiplexer_1_out[2], m);
  xor xor_4 (xor_1_out[3], multiplexer_1_out[3], m);
  xor xor_5 (xor_1_out[4], multiplexer_1_out[4], m);
  xor xor_6 (xor_1_out[5], multiplexer_1_out[5], m);
  xor xor_7 (xor_1_out[6], multiplexer_1_out[6], m);
  xor xor_8 (xor_1_out[7], multiplexer_1_out[7], m);
  xor xor_9 (xor_1_out[8], multiplexer_1_out[8], m);
  xor xor_10 (xor_1_out[9], multiplexer_1_out[9], m);
  xor xor_11 (xor_1_out[10], multiplexer_1_out[10], m);
  xor xor_12 (xor_1_out[11], multiplexer_1_out[11], m);
  ADD12 add12_1 (.out_4(out_6), .out_5(out_5), .out_6(out_7), .b(xor_1_out), .a(in_4), .in_1(m));

  // Notes on the sheet:
  //   b
  //   a
endmodule

module RORC12x1 (
  input  [11:0] in_1,
  input  c_in,
  output c_out,
  output [11:0] out_4
);


  assign c_out = in_1[0];
  assign out_4 = {c_in, in_1[11:1]};

  // Notes on the sheet:
  //   input
  //   output
endmodule

module ROLC12x1 (
  input  c_in,
  input  [11:0] in_2,
  output [11:0] out_3,
  output c_out
);


  assign c_out = in_2[11];
  assign out_3 = {in_2[10:0], c_in};

  // Notes on the sheet:
  //   input
  //   output
endmodule

module ALU12 (
  input  [11:0] in_1,
  input  [11:0] in_2,
  input  c_in,
  input  [3:0] in_4,
  output [11:0] out_5,
  output out_6,
  output out_7
);

  wire addsub12_1_out_6, addsub12_1_out_7, alumap_1_m, alumap_1_ovf_msk, alumap_1_s2, alumap_1_shift,
       multiplexer_2_out, not_1_out, rolc12x1_1_c_out, rorc12x1_1_c_out;
  wire [2:0] alumap_1_o0;
  wire [11:0] addsub12_1_out_5, and_1_out, or_1_out, rolc12x1_1_out_3, rorc12x1_1_out_4, xor_1_out;

  assign and_1_out = in_1 & in_2;  // AND_Gate and_1, 12 bits wide
  ALUMap alumap_1 (
    .s2(alumap_1_s2), .OVF_MSK(alumap_1_ovf_msk), .SHIFT(alumap_1_shift), .m(alumap_1_m),
    .O2(alumap_1_o0[2]), .O1(alumap_1_o0[1]), .O0(alumap_1_o0[0]), .in_1(in_4));
  assign or_1_out = in_1 | in_2;  // OR_Gate or_1, 12 bits wide
  assign xor_1_out = in_1 ^ in_2;  // XOR_Gate xor_1, 12 bits wide
  Multiplexer #(.enable("false"), .select(3), .width(12)) multiplexer_1 (
    .in0(and_1_out), .in1(or_1_out), .in2(xor_1_out), .in3(addsub12_1_out_5), .in4(rorc12x1_1_out_4),
    .in5(rolc12x1_1_out_3), .in6(rolc12x1_1_out_3), .out(out_5), .sel(alumap_1_o0));  // open: in7
  ADDSUB12 addsub12_1 (
    .out_7(addsub12_1_out_7), .out_5(addsub12_1_out_5), .out_6(addsub12_1_out_6), .in_1(in_2), .in_4(in_1),
    .s2(alumap_1_s2), .m(alumap_1_m));
  not not_1 (not_1_out, alumap_1_ovf_msk);
  and and_2 (out_7, addsub12_1_out_6, not_1_out);
  Multiplexer #(.enable("false")) multiplexer_2 (.in0(c_in), .in1(1'b0), .out(multiplexer_2_out), .sel(alumap_1_shift));
  RORC12x1 rorc12x1_1 (.c_out(rorc12x1_1_c_out), .out_4(rorc12x1_1_out_4), .in_1(in_1), .c_in(c_in));
  ROLC12x1 rolc12x1_1 (.c_out(rolc12x1_1_c_out), .out_3(rolc12x1_1_out_3), .in_2(in_1), .c_in(multiplexer_2_out));
  Multiplexer #(.enable("false"), .select(3)) multiplexer_3 (
    .in3(addsub12_1_out_7), .in4(rorc12x1_1_c_out), .in5(rolc12x1_1_c_out), .in6(rolc12x1_1_c_out),
    .out(out_6), .sel(alumap_1_o0));  // open: in0, in1, in2, in7

  // Notes on the sheet:
  //   AND
  //   FUN
  //   OR
  //   XOR
  //   a
  //   s
  //   b
  //   ASL
  //   ROR
  //   ROL
endmodule

module ALUMap (
  input  [3:0] in_1,
  output O2,
  output O1,
  output O0,
  output m,
  output s2,
  output OVF_MSK,
  output SHIFT
);

  wire and_1_out, and_2_out, and_3_out, and_4_out, and_5_out, and_6_out, and_7_out, and_8_out, and_11_out,
       and_12_out, not_1_out, not_2_out, not_3_out, not_4_out, not_5_out, not_6_out, not_7_out, not_8_out,
       not_9_out, not_10_out, not_11_out, not_12_out, not_13_out, not_14_out, not_15_out, not_16_out,
       not_17_out, not_18_out, not_19_out, not_20_out;

  not not_1 (not_1_out, in_1[1]);
  not not_2 (not_2_out, in_1[2]);
  not not_3 (not_3_out, in_1[3]);
  not not_4 (not_4_out, in_1[2]);
  not not_5 (not_5_out, in_1[0]);
  not not_6 (not_6_out, in_1[1]);
  not not_7 (not_7_out, in_1[3]);
  not not_8 (not_8_out, in_1[2]);
  not not_9 (not_9_out, in_1[1]);
  not not_10 (not_10_out, in_1[3]);
  not not_11 (not_11_out, in_1[2]);
  not not_12 (not_12_out, in_1[3]);
  not not_13 (not_13_out, in_1[2]);
  not not_14 (not_14_out, in_1[1]);
  not not_15 (not_15_out, in_1[3]);
  not not_16 (not_16_out, in_1[1]);
  not not_17 (not_17_out, in_1[2]);
  not not_18 (not_18_out, in_1[1]);
  and and_1 (and_1_out, not_1_out, not_2_out, in_1[3]);
  and and_2 (and_2_out, in_1[2], in_1[1], in_1[0]);
  not not_19 (not_19_out, in_1[2]);
  not not_20 (not_20_out, in_1[0]);
  and and_3 (and_3_out, not_3_out, not_4_out);
  and and_4 (and_4_out, not_3_out, in_1[1], not_5_out);
  and and_5 (and_5_out, not_19_out, not_6_out, in_1[0]);
  and and_6 (and_6_out, not_7_out, not_8_out);
  and and_7 (and_7_out, not_7_out, not_9_out, in_1[0]);
  and and_8 (and_8_out, in_1[3], not_8_out, not_9_out, not_20_out);
  and and_9 (m, not_10_out, not_11_out, in_1[0]);
  and and_10 (s2, not_12_out, not_13_out, not_14_out);
  and and_11 (and_11_out, not_15_out, in_1[2], not_16_out);
  and and_12 (and_12_out, not_15_out, in_1[2], in_1[1], in_1[0]);
  and and_13 (SHIFT, in_1[3], not_17_out, not_18_out, in_1[0]);
  or or_1 (O2, and_1_out, and_2_out);
  or or_2 (O1, and_3_out, and_5_out, and_4_out);
  or or_3 (OVF_MSK, and_11_out, and_12_out);
  or or_4 (O0, and_6_out, and_7_out, and_8_out);
endmodule

module ALUDemo (
);

  wire alu12_1_out_6, alu12_1_out_7, dipswitch_2_sw8;
  wire [3:0] dipswitch_2_sw4;
  wire [11:0] alu12_1_out_5, dipswitch_4_sw8, hex_to_7_segment_decoder_3_p1;

  _7_Segment_Display u_7_segment_display_1 ();  // open: g, f, a, b, e, d, c, dp
  // Hex_to_7_Segment_decoder hex_to_7_segment_decoder_1: pin names not known; wires that end beside it: hex_to_7_segment_decoder_3_p1[11:8]
  DipSwitch dipswitch_1 (
    .sw1(hex_to_7_segment_decoder_3_p1[11]), .sw2(hex_to_7_segment_decoder_3_p1[10]),
    .sw3(hex_to_7_segment_decoder_3_p1[9]), .sw4(hex_to_7_segment_decoder_3_p1[8]),
    .sw5(hex_to_7_segment_decoder_3_p1[7]), .sw6(hex_to_7_segment_decoder_3_p1[6]),
    .sw7(hex_to_7_segment_decoder_3_p1[5]), .sw8(hex_to_7_segment_decoder_3_p1[4]));
  _7_Segment_Display u_7_segment_display_2 ();  // open: g, f, a, b, e, d, c, dp
  // Hex_to_7_Segment_decoder hex_to_7_segment_decoder_2: pin names not known; wires that end beside it: hex_to_7_segment_decoder_3_p1[7:4]
  _7_Segment_Display u_7_segment_display_3 ();  // open: g, f, a, b, e, d, c, dp
  // Hex_to_7_Segment_decoder hex_to_7_segment_decoder_3: pin names not known; wires that end beside it: hex_to_7_segment_decoder_3_p1[3:0]
  DipSwitch dipswitch_2 (
    .sw1(dipswitch_2_sw4[3]), .sw2(dipswitch_2_sw4[2]), .sw3(dipswitch_2_sw4[1]), .sw4(dipswitch_2_sw4[0]),
    .sw8(dipswitch_2_sw8));  // open: sw5, sw6, sw7
  DipSwitch dipswitch_3 (
    .sw1(hex_to_7_segment_decoder_3_p1[3]), .sw2(hex_to_7_segment_decoder_3_p1[2]),
    .sw3(hex_to_7_segment_decoder_3_p1[1]), .sw4(hex_to_7_segment_decoder_3_p1[0]),
    .sw5(dipswitch_4_sw8[11]), .sw6(dipswitch_4_sw8[10]), .sw7(dipswitch_4_sw8[9]), .sw8(dipswitch_4_sw8[8]));
  PLA #(.\table ("")) pla (.in(dipswitch_2_sw4));  // open: out
  _7_Segment_Display u_7_segment_display_4 ();  // open: g, f, a, b, e, d, c, dp
  // Hex_to_7_Segment_decoder hex_to_7_segment_decoder_4: pin names not known; wires that end beside it: dipswitch_4_sw8[11:8]
  DipSwitch dipswitch_4 (
    .sw1(dipswitch_4_sw8[7]), .sw2(dipswitch_4_sw8[6]), .sw3(dipswitch_4_sw8[5]), .sw4(dipswitch_4_sw8[4]),
    .sw5(dipswitch_4_sw8[3]), .sw6(dipswitch_4_sw8[2]), .sw7(dipswitch_4_sw8[1]), .sw8(dipswitch_4_sw8[0]));
  _7_Segment_Display u_7_segment_display_5 ();  // open: g, f, a, b, e, d, c, dp
  // Hex_to_7_Segment_decoder hex_to_7_segment_decoder_5: pin names not known; wires that end beside it: dipswitch_4_sw8[7:4]
  _7_Segment_Display u_7_segment_display_6 ();  // open: g, f, a, b, e, d, c, dp
  // Hex_to_7_Segment_decoder hex_to_7_segment_decoder_6: pin names not known; wires that end beside it: dipswitch_4_sw8[3:0]
  ALU12 alu12_1 (
    .out_6(alu12_1_out_6), .out_5(alu12_1_out_5), .out_7(alu12_1_out_7),
    .in_1(hex_to_7_segment_decoder_3_p1), .in_2(dipswitch_4_sw8), .c_in(dipswitch_2_sw8),
    .in_4(dipswitch_2_sw4));
  _7_Segment_Display u_7_segment_display_7 ();  // open: g, f, a, b, e, d, c, dp
  // Hex_to_7_Segment_decoder hex_to_7_segment_decoder_7: pin names not known; wires that end beside it: alu12_1_out_5[11:8]
  _7_Segment_Display u_7_segment_display_8 ();  // open: g, f, a, b, e, d, c, dp
  // Hex_to_7_Segment_decoder hex_to_7_segment_decoder_8: pin names not known; wires that end beside it: alu12_1_out_5[7:4]
  LED led_1 (.in(alu12_1_out_7));
  LED led_2 (.in(alu12_1_out_6));
  _7_Segment_Display u_7_segment_display_9 ();  // open: g, f, a, b, e, d, c, dp
  // Hex_to_7_Segment_decoder hex_to_7_segment_decoder_9: pin names not known; wires that end beside it: alu12_1_out_5[3:0]

  // Notes on the sheet:
  //   cout
  //   ovf
endmodule

module FSMDataPath (
  input  p_load_enable,
  input  [11:0] in_2,
  input  b_load_enable,
  input  in_4,
  input  b_shift_enable,
  input  cf0,
  input  [11:0] af,
  input  in_8,
  input  cf1,
  input  [3:0] in_10,
  output [23:0] out_11,
  output flag,
  output b0
);

  wire and_1_out, and_2_out, clock_1_out, shift_register_1_p2, shift_register_2_p3;
  wire [11:0] register_1_q, shift_register_2_p2;

  Counter #(.max('hc), .width(13)) counter_1 (
    .count(cf0), .carry(flag), .up(1'b1), .clk(clock_1_out), .clr(and_1_out));  // open: load, D, Q
  and and_1 (and_1_out, cf0, cf1);
  Clock clock_1 (.out(clock_1_out));
  and and_2 (and_2_out, p_load_enable, in_4);
  // Shift_Register #(.length(12)) shift_register_1: pin names not known; wires that end beside it: in_4, shift_register_1_p2, clock_1_out, p_load_enable, and_2_out, shift_register_2_p2[11], shift_register_2_p2[10], shift_register_2_p2[9], shift_register_2_p2[8], shift_register_2_p2[7], shift_register_2_p2[6], shift_register_2_p2[5], shift_register_2_p2[4], shift_register_2_p2[3], shift_register_2_p2[2]
  // Shift_Register #(.length(12)) shift_register_2: pin names not known; wires that end beside it: shift_register_2_p2[1], shift_register_2_p2[0], shift_register_2_p3, b_shift_enable, shift_register_2_p3, clock_1_out, b_load_enable, and_2_out, b0
  Register #(.width(12)) register_1 (.D(af), .en(in_8), .Q(register_1_q), .clk(clock_1_out));  // open: clr
  ALU12 alu12_1 (
    .out_6(shift_register_1_p2), .out_5(shift_register_2_p2), .in_1(register_1_q), .in_2(out_11[23:12]),
    .c_in(1'b0), .in_4(in_10));  // open: out_7

  // Notes on the sheet:
  //   counter
  //   pf1
  //   pf0
  //   p shift enable
  //   P
  //   bf1
  //   b_value
  //   bf0
  //   B
  //   a_value
  //   b
  //   p
  //   A
  //   adder
endmodule

module ControlUnit (
  input  start,
  input  b0,
  input  flag,
  output out_4,
  output out_5,
  output out_6,
  output out_7,
  output out_8,
  output out_9,
  output out_10
);

  wire and_1_out, and_2_out, and_3_out, and_4_out, and_5_out, and_6_out, and_7_out, and_8_out, and_9_out,
       and_10_out, and_11_out, clock_1_out, d_ff_1_q, d_ff_2_q, not_1_out, not_2_out, not_3_out, not_4_out,
       not_5_out, not_6_out, or_1_out;

  not not_1 (not_1_out, d_ff_2_q);
  not not_2 (not_2_out, flag);
  not not_3 (not_3_out, d_ff_2_q);
  not not_4 (not_4_out, d_ff_1_q);
  not not_5 (not_5_out, b0);
  not not_6 (not_6_out, flag);
  and and_1 (and_1_out, not_3_out, not_4_out, start, not_5_out, not_6_out);
  and and_2 (and_2_out, not_1_out, d_ff_1_q, start, b0, not_2_out);
  OutputGenerator outputgenerator_1 (
    .cf1(out_8), .pf0(out_5), .bf1(out_6), .bf0(out_7), .out_13(out_10), .pf1(out_4), .cf0(out_9),
    .af(out_9), .q0(d_ff_1_q), .b0(b0), .Flag(flag), .start(start), .q1(d_ff_2_q));
  and and_3 (and_3_out, not_3_out, not_4_out, start, not_5_out, flag);
  Clock clock_1 (.out(clock_1_out));
  and and_4 (and_4_out, not_3_out, not_4_out, start, b0, not_6_out);
  D_Flip_Flop d_ff_1 (.clk(clock_1_out), .D(or_1_out), .Q(d_ff_1_q));  // open: Qn, preset, reset
  D_Flip_Flop d_ff_2 (.clk(clock_1_out), .D(and_2_out), .Q(d_ff_2_q));  // open: Qn, preset, reset
  and and_5 (and_5_out, not_3_out, not_4_out, start, b0, flag);
  and and_6 (and_6_out, not_3_out, d_ff_1_q, start, b0, flag);
  or or_1 (or_1_out, and_1_out, and_3_out, and_4_out, and_5_out, and_6_out, and_7_out, and_8_out, and_10_out, and_9_out, and_11_out);
  and and_7 (and_7_out, not_3_out, d_ff_1_q, start, b0, not_6_out);
  and and_8 (and_8_out, d_ff_2_q, not_4_out, start, not_5_out, not_6_out);
  and and_9 (and_9_out, d_ff_2_q, not_4_out, start, b0, not_6_out);
  and and_10 (and_10_out, d_ff_2_q, not_4_out, start, not_5_out, flag);
  and and_11 (and_11_out, d_ff_2_q, not_4_out, start, b0, flag);

  // Notes on the sheet:
  //   q1
  //   q0
  //   clock
  //   d0
  //   d1
  //   q0
  //   q1
endmodule

module OutputGenerator (
  input  start,
  input  q1,
  input  q0,
  input  b0,
  input  Flag,
  output pf1,
  output pf0,
  output bf1,
  output bf0,
  output cf1,
  output cf0,
  output af,
  output out_13
);

  wire and_1_out, and_2_out, and_4_out, and_5_out, and_6_out, and_7_out, and_9_out, and_10_out, and_11_out,
       and_12_out, not_1_out, not_2_out, not_3_out, not_4_out, not_5_out, not_6_out, not_7_out, not_8_out,
       not_9_out, not_10_out, not_11_out, not_12_out, not_13_out, not_14_out, not_15_out, not_16_out,
       not_17_out, not_18_out, not_19_out, not_20_out, not_21_out, not_22_out, not_23_out, not_24_out,
       not_25_out, not_26_out, not_27_out, not_28_out, not_29_out, not_30_out, not_31_out, not_32_out,
       not_33_out, not_34_out;

  not not_1 (not_1_out, q1);
  not not_2 (not_2_out, b0);
  not not_3 (not_3_out, Flag);
  not not_4 (not_4_out, q1);
  not not_5 (not_5_out, Flag);
  not not_6 (not_6_out, q0);
  not not_7 (not_7_out, Flag);
  not not_8 (not_8_out, q1);
  not not_9 (not_9_out, b0);
  not not_10 (not_10_out, Flag);
  not not_11 (not_11_out, q1);
  not not_12 (not_12_out, Flag);
  not not_13 (not_13_out, q1);
  not not_14 (not_14_out, b0);
  not not_15 (not_15_out, Flag);
  not not_16 (not_16_out, q0);
  not not_17 (not_17_out, Flag);
  not not_18 (not_18_out, q1);
  not not_19 (not_19_out, b0);
  not not_20 (not_20_out, Flag);
  not not_21 (not_21_out, q1);
  not not_22 (not_22_out, b0);
  not not_23 (not_23_out, Flag);
  not not_24 (not_24_out, q1);
  not not_25 (not_25_out, b0);
  not not_26 (not_26_out, Flag);
  not not_27 (not_27_out, q0);
  not not_28 (not_28_out, Flag);
  not not_29 (not_29_out, q1);
  not not_30 (not_30_out, Flag);
  not not_31 (not_31_out, start);
  not not_32 (not_32_out, q1);
  not not_33 (not_33_out, q0);
  not not_34 (not_34_out, b0);
  and and_1 (and_1_out, start, not_1_out, q0, not_2_out, not_3_out);
  and and_2 (and_2_out, start, not_4_out, q0, b0, not_5_out);
  and and_3 (pf0, start, q1, not_6_out, b0, not_7_out);
  and and_4 (and_4_out, start, not_8_out, q0, not_9_out, not_10_out);
  and and_5 (and_5_out, start, not_11_out, q0, b0, not_12_out);
  and and_6 (and_6_out, start, not_13_out, q0, not_14_out, not_15_out);
  and and_7 (and_7_out, start, q1, not_16_out, b0, not_17_out);
  and and_8 (cf1, start, not_18_out, q0, not_19_out, not_20_out);
  and and_9 (and_9_out, start, not_21_out, q0, not_22_out, not_23_out);
  and and_10 (and_10_out, start, not_24_out, q0, not_25_out, not_26_out);
  and and_11 (and_11_out, start, q1, not_27_out, b0, not_28_out);
  and and_12 (and_12_out, start, not_29_out, q0, b0, not_30_out);
  and and_13 (out_13, not_31_out, not_32_out, not_33_out, not_34_out, Flag);
  or or_1 (pf1, and_1_out, and_2_out);
  or or_2 (bf1, and_4_out, and_5_out);
  or or_3 (bf0, and_6_out, and_7_out);
  or or_4 (af, and_9_out, and_10_out, and_11_out, and_12_out);

  assign cf0 = af;

  // Notes on the sheet:
  //   done
endmodule

module MPMultiplier (
  input  start,
  input  [11:0] in_2,
  input  [11:0] in_3,
  output [23:0] out_4
);

  wire clock_1_out, fsmdatapath_1_b0, fsmdatapath_1_flag, multiplexer_1_out, not_1_out;
  wire [2:0] counter_1_q, rom_1_data, rom_1_data_2;
  wire [10:3] rom_1_data_3;

  not not_1 (not_1_out, start);
  Multiplexer #(.enable("false"), .select(3)) multiplexer_1 (
    .in0(1'b0), .in1(1'b1), .in2(not_1_out), .in3(fsmdatapath_1_flag), .in4(fsmdatapath_1_b0),
    .out(multiplexer_1_out), .sel(rom_1_data));  // open: in5, in6, in7
  ROM #(.addrWidth(3), .dataWidth(14)) rom_1 (.addr(counter_1_q), .data({rom_1_data, rom_1_data_3, rom_1_data_2}));
  Clock clock_1 (.out(clock_1_out));
  Counter #(.max('h7), .width(3)) counter_1 (
    .load(multiplexer_1_out), .D(rom_1_data_2), .Q(counter_1_q), .clk(clock_1_out), .clr(rom_1_data_3[3]));  // open: count, carry
  FSMDataPath fsmdatapath_1 (
    .b0(fsmdatapath_1_b0), .out_11(out_4), .flag(fsmdatapath_1_flag), .af(in_3), .in_8(rom_1_data_3[4]),
    .in_10(4'b0000), .cf1(rom_1_data_3[10]), .cf0(rom_1_data_3[9]), .in_4(rom_1_data_3[8]),
    .p_load_enable(rom_1_data_3[7]), .b_shift_enable(rom_1_data_3[6]), .b_load_enable(rom_1_data_3[5]),
    .in_2(in_2));

  // Notes on the sheet:
  //   contents of rom_1 (hex, n*v repeats v):
  //   1000 7b0 1806 2005 80 b42 808
  //   done
endmodule

module FSMMultiplier (
  input  [11:0] in_1,
  input  [11:0] B_value,
  input  start_asyn,
  input  reset,
  output [23:0] out_5,
  output done
);

  wire and_1_out, and_2_out, clock_1_out, controlunit_1_out_4, controlunit_1_out_5, controlunit_1_out_6,
       controlunit_1_out_7, controlunit_1_out_8, controlunit_1_out_9, controlunit_1_out_10, d_ff_1_q,
       fsmdatapath_1_b0, fsmdatapath_1_flag, not_1_out, not_2_out;

  Clock clock_1 (.out(clock_1_out));
  not not_1 (not_1_out, start_asyn);
  D_Flip_Flop d_ff_1 (.clk(clock_1_out), .D(start_asyn), .Q(d_ff_1_q), .reset(and_1_out));  // open: Qn, preset
  and and_1 (and_1_out, reset, not_2_out);
  D_Flip_Flop d_ff_2 (
    .clk(clock_1_out), .D(controlunit_1_out_10), .Q(done), .preset(controlunit_1_out_10), .reset(and_2_out));  // open: Qn
  and and_2 (and_2_out, not_1_out, reset);
  not not_2 (not_2_out, controlunit_1_out_10);
  ControlUnit controlunit_1 (
    .out_10(controlunit_1_out_10), .out_4(controlunit_1_out_4), .out_5(controlunit_1_out_5),
    .out_9(controlunit_1_out_9), .out_8(controlunit_1_out_8), .out_6(controlunit_1_out_6),
    .out_7(controlunit_1_out_7), .flag(fsmdatapath_1_flag), .b0(fsmdatapath_1_b0), .start(d_ff_1_q));
  FSMDataPath fsmdatapath_1 (
    .b0(fsmdatapath_1_b0), .out_11(out_5), .flag(fsmdatapath_1_flag), .af(in_1), .in_8(controlunit_1_out_9),
    .in_10(4'b0000), .cf1(controlunit_1_out_8), .cf0(controlunit_1_out_9), .in_4(controlunit_1_out_4),
    .p_load_enable(controlunit_1_out_5), .b_shift_enable(controlunit_1_out_6),
    .b_load_enable(controlunit_1_out_7), .in_2(B_value));

  // Notes on the sheet:
  //   A_value
endmodule

module MultiplierDemo (
  input  in_1,
  input  in_2,
  input  in_3,
  output out_4
);

  wire [3:0] dipswitch_2_sw8, dipswitch_3_sw8, dipswitch_4_sw8, dipswitch_5_sw4, dipswitch_5_sw8,
       dipswitch_6_sw4, dipswitch_6_sw8, fsmmultiplier_1_out_5, fsmmultiplier_1_out_5_2,
       fsmmultiplier_1_out_5_3, fsmmultiplier_1_out_5_4, fsmmultiplier_1_out_5_5,
       hex_to_7_segment_decoder_1_p1, hex_to_7_segment_decoder_2_p1, hex_to_7_segment_decoder_3_p1,
       hex_to_7_segment_decoder_4_p1, hex_to_7_segment_decoder_6_p1, mpmultiplier_1_out_4,
       mpmultiplier_1_out_4_2, mpmultiplier_1_out_4_3, mpmultiplier_1_out_4_4, mpmultiplier_1_out_4_5,
       mpmultiplier_1_out_4_6;
  wire [23:20] fsmmultiplier_1_out_5_6;

  _7_Segment_Display u_7_segment_display_1 ();  // open: g, f, a, b, e, d, c, dp
  _7_Segment_Display u_7_segment_display_2 ();  // open: g, f, a, b, e, d, c, dp
  // Hex_to_7_Segment_decoder hex_to_7_segment_decoder_1: pin names not known; wires that end beside it: hex_to_7_segment_decoder_1_p1
  // Hex_to_7_Segment_decoder hex_to_7_segment_decoder_2: pin names not known; wires that end beside it: hex_to_7_segment_decoder_2_p1
  DipSwitch dipswitch_1 (
    .sw1(hex_to_7_segment_decoder_1_p1[3]), .sw2(hex_to_7_segment_decoder_1_p1[2]),
    .sw3(hex_to_7_segment_decoder_1_p1[1]), .sw4(hex_to_7_segment_decoder_1_p1[0]),
    .sw5(hex_to_7_segment_decoder_2_p1[3]), .sw6(hex_to_7_segment_decoder_2_p1[2]),
    .sw7(hex_to_7_segment_decoder_2_p1[1]), .sw8(hex_to_7_segment_decoder_2_p1[0]));
  _7_Segment_Display u_7_segment_display_3 ();  // open: g, f, a, b, e, d, c, dp
  // Hex_to_7_Segment_decoder hex_to_7_segment_decoder_3: pin names not known; wires that end beside it: hex_to_7_segment_decoder_3_p1
  DipSwitch dipswitch_2 (
    .sw1(hex_to_7_segment_decoder_3_p1[3]), .sw2(hex_to_7_segment_decoder_3_p1[2]),
    .sw3(hex_to_7_segment_decoder_3_p1[1]), .sw4(hex_to_7_segment_decoder_3_p1[0]), .sw5(dipswitch_2_sw8[3]),
    .sw6(dipswitch_2_sw8[2]), .sw7(dipswitch_2_sw8[1]), .sw8(dipswitch_2_sw8[0]));
  _7_Segment_Display u_7_segment_display_4 ();  // open: g, f, a, b, e, d, c, dp
  // Hex_to_7_Segment_decoder hex_to_7_segment_decoder_4: pin names not known; wires that end beside it: hex_to_7_segment_decoder_4_p1
  DipSwitch dipswitch_3 (
    .sw1(hex_to_7_segment_decoder_4_p1[3]), .sw2(hex_to_7_segment_decoder_4_p1[2]),
    .sw3(hex_to_7_segment_decoder_4_p1[1]), .sw4(hex_to_7_segment_decoder_4_p1[0]), .sw5(dipswitch_3_sw8[3]),
    .sw6(dipswitch_3_sw8[2]), .sw7(dipswitch_3_sw8[1]), .sw8(dipswitch_3_sw8[0]));
  _7_Segment_Display u_7_segment_display_5 ();  // open: g, f, a, b, e, d, c, dp
  _7_Segment_Display u_7_segment_display_6 ();  // open: g, f, a, b, e, d, c, dp
  // Hex_to_7_Segment_decoder hex_to_7_segment_decoder_5: pin names not known; wires that end beside it: dipswitch_2_sw8
  // Hex_to_7_Segment_decoder hex_to_7_segment_decoder_6: pin names not known; wires that end beside it: hex_to_7_segment_decoder_6_p1
  DipSwitch dipswitch_4 (
    .sw1(hex_to_7_segment_decoder_6_p1[3]), .sw2(hex_to_7_segment_decoder_6_p1[2]),
    .sw3(hex_to_7_segment_decoder_6_p1[1]), .sw4(hex_to_7_segment_decoder_6_p1[0]), .sw5(dipswitch_4_sw8[3]),
    .sw6(dipswitch_4_sw8[2]), .sw7(dipswitch_4_sw8[1]), .sw8(dipswitch_4_sw8[0]));
  _7_Segment_Display u_7_segment_display_7 ();  // open: g, f, a, b, e, d, c, dp
  // Hex_to_7_Segment_decoder hex_to_7_segment_decoder_7: pin names not known; wires that end beside it: dipswitch_3_sw8
  DipSwitch dipswitch_5 (
    .sw1(dipswitch_5_sw4[3]), .sw2(dipswitch_5_sw4[2]), .sw3(dipswitch_5_sw4[1]), .sw4(dipswitch_5_sw4[0]),
    .sw5(dipswitch_5_sw8[3]), .sw6(dipswitch_5_sw8[2]), .sw7(dipswitch_5_sw8[1]), .sw8(dipswitch_5_sw8[0]));
  _7_Segment_Display u_7_segment_display_8 ();  // open: g, f, a, b, e, d, c, dp
  // Hex_to_7_Segment_decoder hex_to_7_segment_decoder_8: pin names not known; wires that end beside it: dipswitch_4_sw8
  DipSwitch dipswitch_6 (
    .sw1(dipswitch_6_sw4[3]), .sw2(dipswitch_6_sw4[2]), .sw3(dipswitch_6_sw4[1]), .sw4(dipswitch_6_sw4[0]),
    .sw5(dipswitch_6_sw8[3]), .sw6(dipswitch_6_sw8[2]), .sw7(dipswitch_6_sw8[1]), .sw8(dipswitch_6_sw8[0]));
  _7_Segment_Display u_7_segment_display_9 ();  // open: g, f, a, b, e, d, c, dp
  // Hex_to_7_Segment_decoder hex_to_7_segment_decoder_9: pin names not known; wires that end beside it: dipswitch_5_sw4
  _7_Segment_Display u_7_segment_display_10 ();  // open: g, f, a, b, e, d, c, dp
  // Hex_to_7_Segment_decoder hex_to_7_segment_decoder_10: pin names not known; wires that end beside it: dipswitch_6_sw4
  _7_Segment_Display u_7_segment_display_11 ();  // open: g, f, a, b, e, d, c, dp
  // Hex_to_7_Segment_decoder hex_to_7_segment_decoder_11: pin names not known; wires that end beside it: dipswitch_5_sw8
  _7_Segment_Display u_7_segment_display_12 ();  // open: g, f, a, b, e, d, c, dp
  // Hex_to_7_Segment_decoder hex_to_7_segment_decoder_12: pin names not known; wires that end beside it: dipswitch_6_sw8
  FSMMultiplier fsmmultiplier_1 (
    .out_5({fsmmultiplier_1_out_5_6, fsmmultiplier_1_out_5_5, fsmmultiplier_1_out_5_4, fsmmultiplier_1_out_5_3, fsmmultiplier_1_out_5_2, fsmmultiplier_1_out_5}),
    .done(out_4), .reset(in_2), .start_asyn(in_1),
    .B_value({dipswitch_3_sw8, dipswitch_5_sw4, dipswitch_5_sw8}),
    .in_1({hex_to_7_segment_decoder_1_p1, hex_to_7_segment_decoder_2_p1, hex_to_7_segment_decoder_4_p1}));
  MPMultiplier mpmultiplier_1 (
    .out_4({mpmultiplier_1_out_4_6, mpmultiplier_1_out_4_5, mpmultiplier_1_out_4_4, mpmultiplier_1_out_4_3, mpmultiplier_1_out_4_2, mpmultiplier_1_out_4}),
    .start(in_3), .in_2({dipswitch_4_sw8, dipswitch_6_sw4, dipswitch_6_sw8}),
    .in_3({hex_to_7_segment_decoder_3_p1, dipswitch_2_sw8, hex_to_7_segment_decoder_6_p1}));
  // _7_Segment_Display 7_segment_display_13: pin names not known; wires that end beside it: fsmmultiplier_1_out_5_5, fsmmultiplier_1_out_5_4
  // _7_Segment_Display 7_segment_display_14: pin names not known; wires that end beside it: fsmmultiplier_1_out_5_6, fsmmultiplier_1_out_5_5
  // Hex_to_7_Segment_decoder hex_to_7_segment_decoder_13: pin names not known
  // Hex_to_7_Segment_decoder hex_to_7_segment_decoder_14: pin names not known
  // _7_Segment_Display 7_segment_display_15: pin names not known; wires that end beside it: fsmmultiplier_1_out_5_4, fsmmultiplier_1_out_5_3
  // Hex_to_7_Segment_decoder hex_to_7_segment_decoder_15: pin names not known
  // _7_Segment_Display 7_segment_display_16: pin names not known; wires that end beside it: fsmmultiplier_1_out_5_3, fsmmultiplier_1_out_5_2
  // _7_Segment_Display 7_segment_display_17: pin names not known; wires that end beside it: fsmmultiplier_1_out_5_2, fsmmultiplier_1_out_5
  // Hex_to_7_Segment_decoder hex_to_7_segment_decoder_16: pin names not known
  // Hex_to_7_Segment_decoder hex_to_7_segment_decoder_17: pin names not known
  // _7_Segment_Display 7_segment_display_18: pin names not known; wires that end beside it: mpmultiplier_1_out_4_6, mpmultiplier_1_out_4_5
  // _7_Segment_Display 7_segment_display_19: pin names not known; wires that end beside it: mpmultiplier_1_out_4_5, mpmultiplier_1_out_4_4
  // Hex_to_7_Segment_decoder hex_to_7_segment_decoder_18: pin names not known
  // Hex_to_7_Segment_decoder hex_to_7_segment_decoder_19: pin names not known
  _7_Segment_Display u_7_segment_display_20 ();  // open: g, f, a, b, e, d, c, dp
  // Hex_to_7_Segment_decoder hex_to_7_segment_decoder_20: pin names not known
  // _7_Segment_Display 7_segment_display_21: pin names not known; wires that end beside it: mpmultiplier_1_out_4_4, mpmultiplier_1_out_4_3
  // Hex_to_7_Segment_decoder hex_to_7_segment_decoder_21: pin names not known; wires that end beside it: mpmultiplier_1_out_4_6
  // _7_Segment_Display 7_segment_display_22: pin names not known; wires that end beside it: mpmultiplier_1_out_4_3, mpmultiplier_1_out_4_2
  // _7_Segment_Display 7_segment_display_23: pin names not known; wires that end beside it: mpmultiplier_1_out_4_2, mpmultiplier_1_out_4
  // Hex_to_7_Segment_decoder hex_to_7_segment_decoder_22: pin names not known
  // Hex_to_7_Segment_decoder hex_to_7_segment_decoder_23: pin names not known
  _7_Segment_Display u_7_segment_display_24 ();  // open: g, f, a, b, e, d, c, dp
  // Hex_to_7_Segment_decoder hex_to_7_segment_decoder_24: pin names not known
endmodule
